# Fritzing sketch glove_circuit (saved by Fritzing 0.9.3b)
breadboards: 1

parts:
  Part2 = Adafruit LIS3DH [part_number="Adafruit #2809"]
  Part3 = Arduino MKR WiFi 1010
  R1 = Basic Flex Resistor
  R2 = Resistor [package="2010 [SMD]"]

nets:
  VIN: Part2.VIN, Part3.VCC, R2.Pin_1
  GND: Part2.GND, Part3.GND
  N1: Part2.SCL, Part3.D12_SCL
  N2: Part2.SDA, Part3.D11_SDA
  N3: Part3.A1, R1.Pin_2

notes:
  1K resistror Edit later
  Flex sensor- used to turn on and off the glove
  GLOVE_CIRCUIT

custom parts:
  Adafruit LIS3DH: The LIS3DH is a very popular low power triple-axis accelerometer. It's low-cost, but has just about every 'extra' you'd want in an accelerometer: Three axis sensing, 10-bit precision ±2g/±4g/±8g/±16g selectable scaling Both I2C (2 possible addresses) and SPI interface options Interrupt output Multiple data rate options 1 Hz to 5Khz As low as 2uA current draw (just the chip itself, not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
  Arduino MKR WiFi 1010: This is the newest version of the MKR 1000 WIFI, but with an ESP32 module on board made by U-BLOX.
  Resistor: Resistor Basic schematic elements and footprints for 0603, 1206, and PTH resistors.
